// Digital circuit control.dig as structural Verilog
module control (
  input  CLK,
  input  run,
  input  [4:0] OPC,
  input  Z,
  input  C,
  output [16:0] out,
  output [1:0] cycle_o
);

  wire not_1_out;

  not not_1 (not_1_out, CLK);
  Counter #(.Bits(2)) Cycle (.en(run), .C(not_1_out), .clr(1'b0), .out(cycle_o));  // open: ovf
  ROM #(.AddrBits(9), .Bits(17)) Control (.A({OPC, Z, C, cycle_o}), .sel(1'b1), .D(out));

  // Notes on the sheet:
  //   contents of Control (hex, n*v repeats v):
  //   d400,d200,10000,0,d400,d200,10000,0,d400,d200,10000,0,d400,d200,10000,0,d400,d200,
  //   0,0,d400,d200,0,0,d400,d200,0,0,d400,d200,0,0,d400,d200,0,0,d400,d200,0,0,d400,d200,
  //   0,0,d400,d200,0,0,d400,d200,0,0,d400,d200,0,0,d400,d200,0,0,d400,d200,0,0,d400,d200,
  //   0,0,d400,d200,0,0,d400,d200,0,0,d400,d200,0,0,d400,d200,0,0,d400,d200,0,0,d400,d200,
  //   0,0,d400,d200,0,0,d400,d200,0,0,d400,d200,0,0,d400,d200,0,0,d400,d200,0,0,d400,d200,
  //   0,0,d400,d200,0,0,d400,d200,0,0,d400,d200,0,0,d400,d200,0,0,d400,d200,0,0,d400,d200,
  //   0,0,d400,d200,0,0,d400,d200,0,0,d400,d200,0,0,d400,d200,0,0,d400,d200,0,0,d400,d200,
  //   0,0,d400,d200,0,0,d400,d200,0,0,d400,d200,0,0,d400,d200,0,0,d400,d200,0,0,d400,d200,
  //   0,0,d400,d200,0,0,d400,d200,0,0,d400,d200,0,0,d400,d200,0,0,d400,d200,0,0,d400,d200,
  //   0,0,d400,d200,0,0,d400,d200,0,0,d400,d200,0,0,d400,d200,0,0,d400,d200,0,0,d400,d200,
  //   0,0,d400,d200,0,0,d400,d200,0,0,d400,d200,0,0,d400,d200,0,0,d400,d200,0,0,d400,d200,
  //   0,0,d400,d200,0,0,d400,d200,0,0,d400,d200,0,0,d400,d200,0,0,d400,d200,0,0,d400,d200,
  //   0,0,d400,d200,0,0,d400,d200,0,0,d400,d200,0,0,d400,d200,0,0,d400,d200,0,0,d400,d200,
  //   0,0,d400,d200,0,0,d400,d200,0,0,d400,d200,0,0,d400,d200,0,0,d400,d200,0,0,d400,d200,
  //   0,0,d400,d200,0,0,d400,d200,0,0,d400,d200,0,0,d400,d200,0,0,d400,d200,0,0,d400,d200,
  //   0,0,d400,d200,0,0,d400,d200,0,0,d400,d200,0,0,d400,d200,0,0,d400,d200,0,0,d400,d200,
  //   0,0,d400,d200,0,0,d400,d200,0,0,d400,d200,0,0,d400,d200,0,0,d400,d200,0,0,d400,d200,
  //   0,0,d400,d200,0,0,d400,d200,0,0,d400,d200,0,0,d400,d200,0,0,d400,d200,0,0,d400,d200,
  //   0,0,d400,d200,0,0,d400,d200,0,0,d400,d200,0,0,d400,d200,0,0,d400,d200,0,0,d400,d200,
  //   0,0,d400,d200,0,0,d400,d200,0,0,d400,d200,0,0,d400,d200,0,0,d400,d200,0,0,d400,d200,
  //   0,0,d400,d200,0,0,d400,d200,0,0,d400,d200,0,0,d400,d200,0,0,d400,d200,0,0,d400,d200,
  //   0,0,d400,d200,0,0,d400,d200,0,0,d400,d200
endmodule
