// Digital circuit cpu.dig as structural Verilog
module cpu (
  input  Clock,
  input  PC_inc,
  input  PC_r,
  input  PC_w,
  input  IRH_w,
  input  IRL_w,
  input  DIR_sel,
  input  IMM_sel,
  input  Rs_src,
  input  Rd_w,
  input  Rs_r,
  input  IND_sel,
  input  SPC_r,
  input  SPC_w,
  input  RAM_r,
  input  RAM_w,
  input  ALU_r,
  input  HLT,
  input  auto,
  input  RST,
  input  run,
  output [1:0] Cycle_out,
  output [16:0] control_out,
  output [4:0] Opcode
);

  wire alu_1_c_o, alu_1_z_o, ALU_r_t, CLK, DIR_sel_t, HLT_t, IMM_sel_t, IND_sel_t, instruction_1_p13,
       IRH_w_t, IRL_w_t, PC_inc_t, PC_r_t, PC_w_t, RAM_r_t, RAM_w_t, Rd_w_t, Rs_r_t, Rs_src_t, SPC_r_t,
       SPC_w_t, status_1_c_o, status_1_z_o;
  wire [2:0] instruction_1_p10, instruction_1_p11, instruction_1_p12;
  wire [7:0] pc_1_p1, registers_1_alu_0, registers_1_alu_1;
  wire [15:0] pc_1_p6;

  assign {ALU_r_t, SPC_w_t, SPC_r_t, Rs_r_t, Rd_w_t, Rs_src_t, IND_sel_t, DIR_sel_t, IMM_sel_t, IRL_w_t, IRH_w_t, RAM_w_t, RAM_r_t, PC_w_t, PC_r_t, PC_inc_t, HLT_t} = ~auto ? {ALU_r, SPC_w, SPC_r, Rs_r, Rd_w, Rs_src, IND_sel, DIR_sel, IMM_sel, IRL_w, IRH_w, RAM_w, RAM_r, PC_w, PC_r, PC_inc, HLT} : 17'bz;  // DriverInvSel driverinvsel_1
  and and_1 (CLK, Clock, ~HLT_t);  // And
  // pc pc_1: pin names not known; wires that end beside it: pc_1_p1, PC_inc_t, CLK, PC_r_t, PC_w_t, pc_1_p6, RST, pc_1_p6
  RAMSinglePort #(.AddrBits(16), .isProgramMemory("true"), .Bits(8)) ramsingleport_1 (
    .A(pc_1_p6), .str(RAM_w_t), .C(CLK), .ld(RAM_r_t), .D(pc_1_p1));
  // instruction instruction_1: pin names not known; wires that end beside it: pc_1_p1, CLK, IRH_w_t, IRL_w_t, DIR_sel_t, IMM_sel_t, Rs_src_t, pc_1_p6, pc_1_p1, instruction_1_p10, instruction_1_p11, instruction_1_p12, instruction_1_p13, Opcode
  registers registers_1 (
    .A_in(pc_1_p6), .D_in(pc_1_p1), .CLK(CLK), .R_d(instruction_1_p10), .Rd_w(Rd_w_t),
    .nSt(instruction_1_p13), .R_S0(instruction_1_p11), .Rs_r(Rs_r_t), .R_S1(instruction_1_p12),
    .DIR_sel(DIR_sel_t), .IND_sel(IND_sel_t), .SPC_r(SPC_r_t), .SPC_w(SPC_w_t), .A_out(pc_1_p6),
    .D_out(pc_1_p1), .ALU_0(registers_1_alu_0), .ALU_1(registers_1_alu_1));
  alu alu_1 (
    .ALU_0(registers_1_alu_0), .ALU_1(registers_1_alu_1), .OPC(Opcode), .C_i(status_1_c_o), .ALU_r(ALU_r_t),
    .D_o(pc_1_p1), .Z_o(alu_1_z_o), .C_o(alu_1_c_o));
  status status_1 (.Z_i(alu_1_z_o), .C_i(alu_1_c_o), .en(ALU_r_t), .CLK(CLK), .Z_o(status_1_z_o), .C_o(status_1_c_o));
  control control_1 (
    .CLK(CLK), .run(run), .Z(status_1_z_o), .C(status_1_c_o), .OPC(Opcode), .auto(auto), .cycle_o(Cycle_out),
    .control_o(control_out), .HLT(HLT_t), .PC_inc(PC_inc_t), .PC_r(PC_r_t), .PC_w(PC_w_t), .RAM_r(RAM_r_t),
    .RAM_w(RAM_w_t), .IRH_w(IRH_w_t), .IRL_w(IRL_w_t), .IMM_sel(IMM_sel_t), .DIR_sel(DIR_sel_t),
    .IND_sel(IND_sel_t), .Rs_src(Rs_src_t), .Rd_w(Rd_w_t), .Rs_r(Rs_r_t), .SPC_r(SPC_r_t), .SPC_w(SPC_w_t),
    .ALU_r(ALU_r_t));

  // Notes on the sheet:
  //   Rd_w: Write to destination register
  //   Rs_r: Read from source register
  //   auto: Use the controller (if off can be manual)
endmodule
